# Fritzing sketch all (saved by Fritzing 0.9.3b)
breadboards: 1

parts:
  KEYPAD1 = Membrane Matrix Keypad
  Part1 = Arduino Uno (Rev3) - ICSP
  SP2 = SPEAKER [package=pcb_mount_speaker]
  M2 = DC Motor
  Q2 = TRANSISTOR_NPN [package=to-92]
  D2 = Rectifier Diode [part_number=1N4001 package="300 mil [THT]"]
  R2 = Resistor [tolerance=±5% resistance=220 package=THT]
  Part5 = 12 NeoPixel Ring [part_number=1643]

nets:
  N1: KEYPAD1.1, Part1.A0
  N2: KEYPAD1.2, Part1.D6_PWM
  N3: KEYPAD1.3, Part1.D7
  N4: KEYPAD1.4, Part1.D8
  N5: KEYPAD1.5, Part1.D9_PWM
  N6: KEYPAD1.6, Part1.D10_PWM/SS
  N7: KEYPAD1.7, Part1.D11_PWM/MOSI
  N8: Part1.A1, Part5.IN
  GND: Part1.GND, SP2.+, Q2.E, Part5.GND
  N9: Part1.D2, R2.Pin_0
  N10: Part1.D4, SP2.-
  5V: Part1.5V, M2.pin_1, D2.anode, Part5.VDD
  N11: M2.pin_2, Q2.C, D2.cathode
  N12: Q2.B, R2.Pin_1

notes:
  Please note that our keypad is 3x5 and has 8 pins. The last pin connects to pin 12 on Arduino.

custom parts:
  Membrane Matrix Keypad: Membrane Matrix 3x4 Keypad
  12 NeoPixel Ring: 12 ultra bright smart LED NeoPixels are arranged in a circle with 1.5" (37mm) outer diameter. The rings are 'chainable' - connect the output pin of one to the input pin of another. Use only one microcontroller pin to control as many as you can chain together! Each LED is addressable as the driver chip is inside the LED. Each one has ~18mA constant current drive so the color will be very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
