# Fritzing sketch keypad (saved by Fritzing 0.9.3b)

parts:
  KEYPAD1 = Membrane Matrix Keypad
  Part1 = Arduino Uno (Rev3) - ICSP

nets:
  N1: KEYPAD1.1, Part1.A0
  N2: KEYPAD1.2, Part1.D6_PWM
  N3: KEYPAD1.3, Part1.D7
  N4: KEYPAD1.4, Part1.D8
  N5: KEYPAD1.5, Part1.D9_PWM
  N6: KEYPAD1.6, Part1.D10_PWM/SS
  N7: KEYPAD1.7, Part1.D11_PWM/MOSI

notes:
  Please note that our keypad is 3x5 and has 8 pins. The last pin connects to pin 12 on Arduino.

custom parts:
  Membrane Matrix Keypad: Membrane Matrix 3x4 Keypad
